// Logisim project 16-Bit Computer MiniProject.circ as structural Verilog: 13 circuits, main circuit Bit
module Bit (
  input  IN,
  input  LOAD,
  input  CLK,
  output OUT
);

  wire multiplexer_1_out;

  Multiplexer #(.disabled(0), .enable("false")) multiplexer_1 (
    .in0(OUT), .in1(IN), .out(multiplexer_1_out), .sel(LOAD));
  D_Flip_Flop d_ff_1 (.clk(CLK), .D(multiplexer_1_out), .Q(OUT));  // open: Qn, preset, en, reset
endmodule

module Register (
  input  LOAD,
  input  [15:0] IN,
  input  CLK,
  output [15:0] OUT
);

  Bit bit_1 (.IN(IN[0]), .OUT(OUT[0]), .LOAD(LOAD), .CLK(CLK));
  Bit bit_2 (.IN(IN[1]), .OUT(OUT[1]), .LOAD(LOAD), .CLK(CLK));
  Bit bit_3 (.IN(IN[2]), .OUT(OUT[2]), .LOAD(LOAD), .CLK(CLK));
  Bit bit_4 (.IN(IN[3]), .OUT(OUT[3]), .LOAD(LOAD), .CLK(CLK));
  Bit bit_5 (.IN(IN[4]), .OUT(OUT[4]), .LOAD(LOAD), .CLK(CLK));
  Bit bit_6 (.IN(IN[5]), .OUT(OUT[5]), .LOAD(LOAD), .CLK(CLK));
  Bit bit_7 (.IN(IN[6]), .OUT(OUT[6]), .LOAD(LOAD), .CLK(CLK));
  Bit bit_8 (.IN(IN[7]), .OUT(OUT[7]), .LOAD(LOAD), .CLK(CLK));
  Bit bit_9 (.IN(IN[8]), .OUT(OUT[8]), .LOAD(LOAD), .CLK(CLK));
  Bit bit_10 (.IN(IN[9]), .OUT(OUT[9]), .LOAD(LOAD), .CLK(CLK));
  Bit bit_11 (.IN(IN[10]), .OUT(OUT[10]), .LOAD(LOAD), .CLK(CLK));
  Bit bit_12 (.IN(IN[11]), .OUT(OUT[11]), .LOAD(LOAD), .CLK(CLK));
  Bit bit_13 (.IN(IN[12]), .OUT(OUT[12]), .LOAD(LOAD), .CLK(CLK));
  Bit bit_14 (.IN(IN[13]), .OUT(OUT[13]), .LOAD(LOAD), .CLK(CLK));
  Bit bit_15 (.IN(IN[14]), .OUT(OUT[14]), .LOAD(LOAD), .CLK(CLK));
  Bit bit_16 (.IN(IN[15]), .OUT(OUT[15]), .LOAD(LOAD), .CLK(CLK));
endmodule

module RAM8 (
  input  [15:0] IN,
  input  LOAD,
  input  CLK,
  input  [2:0] ADDRESS,
  output [15:0] OUT
);

  wire demultiplexer_1_out0, demultiplexer_1_out1, demultiplexer_1_out2, demultiplexer_1_out3,
       demultiplexer_1_out4, demultiplexer_1_out5, demultiplexer_1_out6, demultiplexer_1_out7;
  wire [15:0] register_1_out, register_2_out, register_3_out, register_4_out, register_5_out, register_6_out,
       register_7_out, register_8_out;

  Demultiplexer #(.select(3), .enable("false")) demultiplexer_1 (
    .out0(demultiplexer_1_out0), .out1(demultiplexer_1_out1), .out2(demultiplexer_1_out2),
    .out3(demultiplexer_1_out3), .out4(demultiplexer_1_out4), .out5(demultiplexer_1_out5),
    .out6(demultiplexer_1_out6), .out7(demultiplexer_1_out7), .in(LOAD), .sel(ADDRESS));
  Register register_1 (.IN(IN), .OUT(register_1_out), .LOAD(demultiplexer_1_out0), .CLK(CLK));
  Register register_2 (.IN(IN), .OUT(register_2_out), .LOAD(demultiplexer_1_out1), .CLK(CLK));
  Register register_3 (.IN(IN), .OUT(register_3_out), .LOAD(demultiplexer_1_out2), .CLK(CLK));
  Register register_4 (.IN(IN), .OUT(register_4_out), .LOAD(demultiplexer_1_out3), .CLK(CLK));
  Register register_5 (.IN(IN), .OUT(register_5_out), .LOAD(demultiplexer_1_out4), .CLK(CLK));
  Register register_6 (.IN(IN), .OUT(register_6_out), .LOAD(demultiplexer_1_out5), .CLK(CLK));
  Register register_7 (.IN(IN), .OUT(register_7_out), .LOAD(demultiplexer_1_out6), .CLK(CLK));
  Register register_8 (.IN(IN), .OUT(register_8_out), .LOAD(demultiplexer_1_out7), .CLK(CLK));
  Multiplexer #(.select(3), .width(16), .enable("false")) multiplexer_1 (
    .in0(register_1_out), .in1(register_2_out), .in2(register_3_out), .in3(register_4_out),
    .in4(register_5_out), .in5(register_6_out), .in6(register_7_out), .in7(register_8_out), .out(OUT),
    .sel(ADDRESS));
endmodule

module RAM64 (
  input  [15:0] IN,
  input  LOAD,
  input  [5:0] in_3,
  input  CLK,
  output [15:0] OUT
);

  wire demultiplexer_1_out0, demultiplexer_1_out1, demultiplexer_1_out2, demultiplexer_1_out3,
       demultiplexer_1_out4, demultiplexer_1_out5, demultiplexer_1_out6, demultiplexer_1_out7;
  wire [15:0] ram8_1_out, ram8_2_out, ram8_3_out, ram8_4_out, ram8_5_out, ram8_6_out, ram8_7_out, ram8_8_out;

  Demultiplexer #(.select(3), .enable("false")) demultiplexer_1 (
    .out0(demultiplexer_1_out0), .out1(demultiplexer_1_out1), .out2(demultiplexer_1_out2),
    .out3(demultiplexer_1_out3), .out4(demultiplexer_1_out4), .out5(demultiplexer_1_out5),
    .out6(demultiplexer_1_out6), .out7(demultiplexer_1_out7), .in(LOAD), .sel(in_3[5:3]));
  RAM8 ram8_1 (.IN(IN), .LOAD(demultiplexer_1_out0), .OUT(ram8_1_out), .CLK(CLK), .ADDRESS(in_3[2:0]));
  RAM8 ram8_2 (.IN(IN), .LOAD(demultiplexer_1_out1), .OUT(ram8_2_out), .CLK(CLK), .ADDRESS(in_3[2:0]));
  RAM8 ram8_3 (.IN(IN), .LOAD(demultiplexer_1_out2), .OUT(ram8_3_out), .CLK(CLK), .ADDRESS(in_3[2:0]));
  RAM8 ram8_4 (.IN(IN), .LOAD(demultiplexer_1_out3), .OUT(ram8_4_out), .CLK(CLK), .ADDRESS(in_3[2:0]));
  RAM8 ram8_5 (.IN(IN), .LOAD(demultiplexer_1_out4), .OUT(ram8_5_out), .CLK(CLK), .ADDRESS(in_3[2:0]));
  RAM8 ram8_6 (.IN(IN), .LOAD(demultiplexer_1_out5), .OUT(ram8_6_out), .CLK(CLK), .ADDRESS(in_3[2:0]));
  RAM8 ram8_7 (.IN(IN), .LOAD(demultiplexer_1_out6), .OUT(ram8_7_out), .CLK(CLK), .ADDRESS(in_3[2:0]));
  RAM8 ram8_8 (.IN(IN), .LOAD(demultiplexer_1_out7), .OUT(ram8_8_out), .CLK(CLK), .ADDRESS(in_3[2:0]));
  Multiplexer #(.select(3), .width(16), .enable("false")) multiplexer_1 (
    .in0(ram8_1_out), .in1(ram8_2_out), .in2(ram8_3_out), .in3(ram8_4_out), .in4(ram8_5_out),
    .in5(ram8_6_out), .in6(ram8_7_out), .in7(ram8_8_out), .out(OUT), .sel(in_3[5:3]));
endmodule

module RAM16K (
  input  [13:0] Address,
  input  [15:0] Input,
  input  Load,
  input  CLK,
  output [15:0] Output
);

  RAM #(.addrWidth(14), .dataWidth(16), .bus("separate")) ram_1 (
    .addr(Address), .din(Input), .data(Output), .str(Load), .clk(CLK), .ld(1'b1));  // open: sel, clr
endmodule

module Display (
  input  [12:0] Address,
  input  [15:0] Input,
  input  Load,
  input  CLK
);

  RAM #(.addrWidth(13), .dataWidth(16), .bus("separate")) ram_1 (
    .addr(Address), .din(Input), .str(Load), .clk(CLK), .ld(1'b1));  // open: data, sel, clr
endmodule

module Memory (
  input  [15:0] IN,
  input  LOAD,
  input  [14:0] Address,
  input  CLK,
  output [15:0] OUT
);

  wire demultiplexer_1_out0, demultiplexer_1_out1, demultiplexer_2_out0;
  wire [6:0] keyboard_1_data;
  wire [15:0] multiplexer_1_out, ram_1_data, ram_2_data;

  Demultiplexer #(.disabled(0), .enable("false")) demultiplexer_1 (
    .out0(demultiplexer_1_out0), .out1(demultiplexer_1_out1), .in(LOAD), .sel(Address[14]));
  Demultiplexer #(.disabled(0), .enable("false")) demultiplexer_2 (
    .out0(demultiplexer_2_out0), .in(demultiplexer_1_out1), .sel(Address[13]));  // open: out1
  Keyboard #(.buflen(8)) keyboard_1 (.clk(CLK), .data(keyboard_1_data));  // open: re, clr, avail
  RAM #(.addrWidth(14), .dataWidth(16), .bus("separate")) ram_1 (
    .addr(Address[13:0]), .din(IN), .data(ram_1_data), .str(demultiplexer_1_out0), .clk(CLK), .ld(1'b1));  // open: sel, clr
  RAM #(.addrWidth(13), .dataWidth(16), .bus("separate")) ram_2 (
    .addr(Address[12:0]), .din(IN), .data(ram_2_data), .str(demultiplexer_2_out0), .clk(CLK), .ld(1'b1));  // open: sel, clr
  Multiplexer #(.width(16), .enable("false")) multiplexer_1 (
    .in0(ram_2_data), .in1({{9{1'b0}}, keyboard_1_data}), .out(multiplexer_1_out), .sel(Address[13]));
  Multiplexer #(.width(16), .enable("false")) multiplexer_2 (
    .in0(ram_1_data), .in1(multiplexer_1_out), .out(OUT), .sel(Address[14]));
endmodule

module ProgramCounter (
  input  CLK,
  input  INC,
  input  [15:0] IN,
  input  LOAD,
  input  RESET,
  output [15:0] OUT
);

  wire [15:0] multiplexer_1_out, multiplexer_2_out, multiplexer_3_out, n16_bit_adder_1_out;

  Register register_1 (.IN(multiplexer_3_out), .OUT(OUT), .LOAD(1'b1), .CLK(CLK));
  _16_Bit_Adder u_16_bit_adder_1 (.Out(n16_bit_adder_1_out), .A(OUT), .B(16'h1));
  Multiplexer #(.width(16), .disabled(0), .enable("false")) multiplexer_1 (
    .in0(OUT), .in1(n16_bit_adder_1_out), .out(multiplexer_1_out), .sel(INC));
  Multiplexer #(.width(16), .disabled(0), .enable("false")) multiplexer_2 (
    .in0(multiplexer_1_out), .in1(IN), .out(multiplexer_2_out), .sel(LOAD));
  Multiplexer #(.width(16), .disabled(0), .enable("false")) multiplexer_3 (
    .in0(multiplexer_2_out), .in1({16{1'b0}}), .out(multiplexer_3_out), .sel(RESET));
endmodule

module FA (
  input  A,
  input  B,
  input  C,
  output Sum,
  output Cout
);

  wire and_1_out, and_2_out, xor_1_out;

  xor xor_1 (xor_1_out, A, B);
  and and_1 (and_1_out, A, B);
  xor xor_2 (Sum, xor_1_out, C);
  and and_2 (and_2_out, xor_1_out, C);
  or or_1 (Cout, and_2_out, and_1_out);
endmodule

module _16_Bit_Adder (
  input  [15:0] A,
  input  [15:0] B,
  output [15:0] Out
);

  wire fa_2_cout, fa_3_cout, fa_4_cout, fa_5_cout, fa_6_cout, fa_7_cout, fa_8_cout, fa_9_cout, fa_10_cout,
       fa_11_cout, fa_12_cout, fa_13_cout, fa_14_cout, fa_15_cout, fa_16_cout;

  FA fa_1 (.A(B[15]), .B(A[15]), .C(fa_2_cout), .Sum(Out[15]));  // open: Cout
  FA fa_2 (.A(B[14]), .B(A[14]), .C(fa_3_cout), .Sum(Out[14]), .Cout(fa_2_cout));
  FA fa_3 (.A(B[13]), .B(A[13]), .C(fa_4_cout), .Sum(Out[13]), .Cout(fa_3_cout));
  FA fa_4 (.A(B[12]), .B(A[12]), .C(fa_5_cout), .Sum(Out[12]), .Cout(fa_4_cout));
  FA fa_5 (.A(B[11]), .B(A[11]), .C(fa_6_cout), .Sum(Out[11]), .Cout(fa_5_cout));
  FA fa_6 (.A(B[10]), .B(A[10]), .C(fa_8_cout), .Sum(Out[10]), .Cout(fa_6_cout));
  FA fa_7 (.A(B[8]), .B(A[8]), .C(fa_9_cout), .Sum(Out[8]), .Cout(fa_7_cout));
  FA fa_8 (.A(B[9]), .B(A[9]), .C(fa_7_cout), .Sum(Out[9]), .Cout(fa_8_cout));
  FA fa_9 (.A(B[7]), .B(A[7]), .C(fa_10_cout), .Sum(Out[7]), .Cout(fa_9_cout));
  FA fa_10 (.A(B[6]), .B(A[6]), .C(fa_11_cout), .Sum(Out[6]), .Cout(fa_10_cout));
  FA fa_11 (.A(B[5]), .B(A[5]), .C(fa_12_cout), .Sum(Out[5]), .Cout(fa_11_cout));
  FA fa_12 (.A(B[4]), .B(A[4]), .C(fa_13_cout), .Sum(Out[4]), .Cout(fa_12_cout));
  FA fa_13 (.A(B[3]), .B(A[3]), .C(fa_14_cout), .Sum(Out[3]), .Cout(fa_13_cout));
  FA fa_14 (.A(B[2]), .B(A[2]), .C(fa_15_cout), .Sum(Out[2]), .Cout(fa_14_cout));
  FA fa_15 (.A(B[1]), .B(A[1]), .C(fa_16_cout), .Sum(Out[1]), .Cout(fa_15_cout));
  FA fa_16 (.A(B[0]), .B(A[0]), .C(1'b0), .Sum(Out[0]), .Cout(fa_16_cout));
endmodule

module ALU (
  input  ZX,
  input  NX,
  input  [15:0] X,
  input  ZY,
  input  NY,
  input  [15:0] Y,
  input  F,
  input  NO,
  output [15:0] out_9,
  output NG,
  output ZR
);

  wire [15:0] and_1_out, multiplexer_1_out, multiplexer_2_out, multiplexer_4_out, n16_bit_adder_1_out,
       not_1_out, not_2_out, not_3_out;

  nor nor_1 (ZR, out_9[8], NG, out_9[14], out_9[13], out_9[12], out_9[11], out_9[10], out_9[9], out_9[7], out_9[6], out_9[5], out_9[4], out_9[3], out_9[2], out_9[1], out_9[0]);
  assign not_1_out = ~X;  // NOT_Gate not_1, 16 bits wide
  Multiplexer #(.select(2), .width(16), .disabled(0), .enable("false")) multiplexer_1 (
    .in0(X), .in1(not_1_out), .in2({16{1'b0}}), .in3({16{1'b1}}), .out(multiplexer_1_out), .sel({ZX, NX}));
  _16_Bit_Adder u_16_bit_adder_1 (.Out(n16_bit_adder_1_out), .A(multiplexer_4_out), .B(multiplexer_1_out));
  Multiplexer #(.width(16), .disabled(0), .enable("false")) multiplexer_2 (
    .in0(and_1_out), .in1(n16_bit_adder_1_out), .out(multiplexer_2_out), .sel(F));
  assign not_2_out = ~multiplexer_2_out;  // NOT_Gate not_2, 16 bits wide
  Multiplexer #(.width(16), .disabled(0), .enable("false")) multiplexer_3 (
    .in0(multiplexer_2_out), .in1(not_2_out), .out({NG, out_9[14:0]}), .sel(NO));
  assign not_3_out = ~Y;  // NOT_Gate not_3, 16 bits wide
  assign and_1_out = multiplexer_1_out & multiplexer_4_out;  // AND_Gate and_1, 16 bits wide
  Multiplexer #(.select(2), .width(16), .disabled(0), .enable("false")) multiplexer_4 (
    .in0(Y), .in1(not_3_out), .in2({16{1'b0}}), .in3({16{1'b1}}), .out(multiplexer_4_out), .sel({ZY, NY}));

  assign out_9[15] = NG;
endmodule

module CPU (
  input  [15:0] InM,
  input  [15:0] Instruction,
  input  CLK,
  input  Reset,
  output [14:0] AddressM,
  output [15:0] OutM,
  output [14:0] PC,
  output WriteM
);

  wire alu_1_ng, alu_1_zr, and_1_out, and_3_out, and_4_out, and_5_out, and_6_out, and_7_out, nor_1_out,
       not_1_out, not_2_out, or_1_out, or_2_out;
  wire [15:0] D_Register_out, multiplexer_1_out, multiplexer_2_out;
  wire [15:15] A_Register_out, programcounter_1_out;

  Multiplexer #(.width(16), .disabled(0), .enable("false")) multiplexer_1 (
    .in0(Instruction), .in1(OutM), .out(multiplexer_1_out), .sel(Instruction[15]));
  not not_1 (not_1_out, Instruction[15]);
  and and_1 (and_1_out, Instruction[15], Instruction[5]);
  and and_2 (WriteM, Instruction[3], Instruction[15]);
  or or_1 (or_1_out, not_1_out, and_1_out);
  and and_3 (and_3_out, Instruction[4], Instruction[15]);
  Register D_Register (.IN(OutM), .OUT(D_Register_out), .LOAD(and_3_out), .CLK(CLK));
  Register A_Register (.IN(multiplexer_1_out), .OUT({A_Register_out[15], AddressM}), .LOAD(or_1_out), .CLK(CLK));
  Multiplexer #(.width(16), .disabled(0), .enable("false")) multiplexer_2 (
    .in0({A_Register_out[15], AddressM}), .in1(InM), .out(multiplexer_2_out), .sel(Instruction[12]));
  ProgramCounter programcounter_1 (
    .INC(not_2_out), .LOAD(and_7_out), .RESET(Reset), .OUT({programcounter_1_out[15], PC}),
    .IN({A_Register_out[15], AddressM}), .CLK(CLK));
  not not_2 (not_2_out, and_7_out);
  ALU alu_1 (
    .ZX(Instruction[11]), .NX(Instruction[10]), .X(D_Register_out), .ZY(Instruction[9]), .NY(Instruction[8]),
    .Y(multiplexer_2_out), .F(Instruction[7]), .NO(Instruction[6]), .ZR(alu_1_zr), .out_9(OutM), .NG(alu_1_ng));
  and and_4 (and_4_out, alu_1_ng, Instruction[2]);
  and and_5 (and_5_out, Instruction[1], alu_1_zr);
  nor nor_1 (nor_1_out, and_5_out, and_4_out);
  and and_6 (and_6_out, nor_1_out, Instruction[0]);
  or or_2 (or_2_out, and_5_out, and_6_out, and_4_out);
  and and_7 (and_7_out, Instruction[15], or_2_out);

  // Other names for the same wires on the sheet: ALU_O[15:0] = OutM
endmodule

module Computer (
  input  Reset
);

  wire CLK_2_out, CLK_out, demultiplexer_1_out0, demultiplexer_1_out1, demultiplexer_2_out0, LOAD;
  wire [6:0] keyboard_1_data;
  wire [14:0] cpu_1_pc, RAM_Address_In;
  wire [15:0] multiplexer_1_out, ram_1_data, ram_2_data, RAM_Value_In, RamOut, rom_1_data;

  ROM #(.addrWidth(15), .dataWidth(16)) rom_1 (.addr(cpu_1_pc), .data(rom_1_data));  // open: sel
  // Probe on RAM_Value_In
  // Probe on RAM_Address_In
  Demultiplexer #(.disabled(0), .enable("false")) demultiplexer_1 (
    .out0(demultiplexer_1_out0), .out1(demultiplexer_1_out1), .in(LOAD), .sel(RAM_Address_In[14]));
  Demultiplexer #(.disabled(0), .enable("false")) demultiplexer_2 (
    .out0(demultiplexer_2_out0), .in(demultiplexer_1_out1), .sel(RAM_Address_In[13]));  // open: out1
  Clock CLK (.out(CLK_out));
  CPU cpu_1 (
    .Instruction(rom_1_data), .CLK(CLK_out), .Reset(Reset), .AddressM(RAM_Address_In), .OutM(RAM_Value_In),
    .PC(cpu_1_pc), .WriteM(LOAD), .InM(RamOut));
  Keyboard #(.buflen(8)) keyboard_1 (.clk(CLK_2_out), .data(keyboard_1_data));  // open: re, clr, avail
  Clock CLK_2 (.out(CLK_2_out));
  RAM #(.addrWidth(14), .dataWidth(16), .bus("separate")) ram_1 (
    .addr(RAM_Address_In[13:0]), .din(RAM_Value_In), .data(ram_1_data), .str(demultiplexer_1_out0),
    .clk(CLK_2_out), .ld(1'b1));  // open: sel, clr
  RAM #(.addrWidth(13), .dataWidth(16), .bus("separate")) ram_2 (
    .addr(RAM_Address_In[12:0]), .din(RAM_Value_In), .data(ram_2_data), .str(demultiplexer_2_out0),
    .clk(CLK_2_out), .ld(1'b1));  // open: sel, clr
  Multiplexer #(.width(16), .enable("false")) multiplexer_1 (
    .in0(ram_2_data), .in1({{9{1'b0}}, keyboard_1_data}), .out(multiplexer_1_out), .sel(RAM_Address_In[13]));
  // Probe on RamOut
  Multiplexer #(.width(16), .enable("false")) multiplexer_2 (
    .in0(ram_1_data), .in1(multiplexer_1_out), .out(RamOut), .sel(RAM_Address_In[14]));

  // Notes on the sheet:
  //   contents of rom_1 (hex, n*v repeats v):
  //   0 fc10 1 f4d0 a e301 1 fc10 c ea87 0 fc10 2 e308 e ea87
  //   RAM
  //   DISPLAY
  //   KEYBOARD
endmodule
